# Fritzing sketch Desktrunk-pcb (saved by Fritzing 0.9.3b)
circuit board: 6.63793cm x 4.3402cm
breadboards: 1

parts:
  PN532-PWR = male pin header, 2 pins [form="♂ (male)"]
  ULN2003-PWR = male pin header, 2 pins [form="♂ (male)"]
  BUTTON = male pin header, 2 pins [form="♂ (male)"]
  ESP32 = node32s
  ESP32-2 = male pin header, 19 pins [form="♂ (male)"]
  ESP32-1 = male pin header, 19 pins [form="♂ (male)"]
  R-BUTTON = Resistor [tolerance=±5% resistance=220 package=THT]
  ULN2003 = ULN2003A breakout board
  Button = Round Pushbutton
  PN532-GPIO = male pin header, 4 pins [form="♂ (male)"]
  ULN2003-GPIO = male pin header, 4 pins [form="♂ (male)"]
  R-LED-G = Resistor [tolerance=±5% resistance=220 package=THT]
  R-LED-B = Resistor [tolerance=±5% resistance=220 package=THT]
  R-LED-R = Resistor [tolerance=±5% resistance=220 package=THT]
  LED = RGB LED - (4 legs) [package="5 mm [THT]"]
  LED-RGB = male pin header, 4 pins [form="♂ (male)"]
  USB = male pin header, 4 pins [form="♂ (male)"]
  BUTTON-PWR = male pin header, 2 pins [form="♂ (male)"]
  ESP32-USB = male pin header, 4 pins [form="♂ (male)"]

nets:
  N1: PN532-PWR.pin1, ULN2003-PWR.pin1, BUTTON.pin1, ULN2003.0V, Button.leg0, USB.pin1, ESP32-USB.pin1
  N2: PN532-PWR.pin2, ULN2003-PWR.pin2, R-BUTTON.Pin_1, ULN2003.+5V, BUTTON-PWR.pin1, ESP32-USB.pin4
  N3: BUTTON.pin2, ESP32.IO21, ESP32-1.pin6, R-BUTTON.Pin_0, Button.leg1
  N4: ESP32.3.3V, ESP32-2.pin1
  N5: ESP32.CHIP_PU, ESP32-2.pin2
  N6: ESP32.IO36, ESP32-2.pin3
  N7: ESP32.IO39, ESP32-2.pin4
  N8: ESP32.IO34, ESP32-2.pin5
  N9: ESP32.IO35, ESP32-2.pin6
  N10: ESP32.IO32, ESP32-2.pin7
  N11: ESP32.IO33, ESP32-2.pin8
  N12: ESP32.IO25, ESP32-2.pin9, R-LED-B.Pin_0
  N13: ESP32.IO26, ESP32-2.pin10, R-LED-G.Pin_0
  N14: ESP32.IO27, ESP32-2.pin11, R-LED-R.Pin_0
  N15: ESP32.IO14, ESP32-2.pin12
  N16: ESP32.IO12, ESP32-2.pin13
  N17: ESP32.V_BATT, ESP32-2.pin14
  N18: ESP32.IO13, ESP32-2.pin15
  N19: ESP32.IO9, ESP32-2.pin16
  N20: ESP32.IO10, ESP32-2.pin17
  N21: ESP32.IO11, ESP32-2.pin18
  N22: ESP32.5V, ESP32-2.pin19
  N23: ESP32.GND, ESP32-1.pin1, ESP32-1.pin7, LED.common_anode, LED-RGB.pin3
  N24: ESP32.IO23, ESP32-1.pin2, PN532-GPIO.pin1
  N25: ESP32.IO22, ESP32-1.pin3
  N26: ESP32.TXD, ESP32-1.pin4
  N27: ESP32.RXD, ESP32-1.pin5
  N28: ESP32.IO19, ESP32-1.pin8, PN532-GPIO.pin2
  N29: ESP32.IO18, ESP32-1.pin9, PN532-GPIO.pin3
  N30: ESP32.IO5, ESP32-1.pin10, PN532-GPIO.pin4
  N31: ESP32.IO17, ESP32-1.pin11
  N32: ESP32.IO16, ESP32-1.pin12
  N33: ESP32.IO4, ESP32-1.pin13, ULN2003.In_4, ULN2003-GPIO.pin1
  N34: ESP32.IO0, ESP32-1.pin14, ULN2003.In_3, ULN2003-GPIO.pin2
  N35: ESP32.IO2, ESP32-1.pin15, ULN2003.In_2, ULN2003-GPIO.pin3
  N36: ESP32.IO15, ESP32-1.pin16, ULN2003.In_1, ULN2003-GPIO.pin4
  N37: ESP32.IO8, ESP32-1.pin17
  N38: ESP32.IO7, ESP32-1.pin18
  N39: ESP32.IO6, ESP32-1.pin19
  N40: R-LED-G.Pin_1, LED.green_cathode, LED-RGB.pin2
  N41: R-LED-B.Pin_1, LED.blue_cathode, LED-RGB.pin1
  N42: R-LED-R.Pin_1, LED.red_cathode, LED-RGB.pin4
  N43: USB.pin2, ESP32-USB.pin2
  N44: USB.pin3, ESP32-USB.pin3
  N45: USB.pin4, BUTTON-PWR.pin2

notes:
  Desktrunk 1 - 2019
  VCC
  +
  GND
  data-
  data+
  R
  G
  B
  IN4
  IN3
  IN2
  IN1
  SCK
  MISO
  SS
  MOSI
  L
  1

custom parts:
  ULN2003A breakout board: ULN2003A 7-way Darlington Transistor Driver on breakoutboard
